# Fritzing sketch GardenaDouble_ESP - v2.2 (saved by Fritzing 0.9.3b)
circuit board: 6cm x 5.5cm
breadboards: 1

parts:
  IC3 = L293D [package=THT]
  R9 = Resistor [tolerance=±5% resistance=100 package=THT]
  R10 = Resistor [tolerance=±5% resistance=100 package=THT]
  R11 = Resistor [tolerance=±5% resistance=10 package=THT]
  R12 = Resistor [tolerance=±5% resistance=10 package=THT]
  D5 = Rectifier Diode [part_number=1N4001 package="300 mil [THT]"]
  D6 = Rectifier Diode [part_number=1N4001 package="300 mil [THT]"]
  JP1 = Header 4 [package=screwterminal-3.5mm-4_lock]
  Part1 = U3V12F9 9V Step-Up Voltage Regulator [part_number=U3V12F9]
  OLED = female pin header, 4 pins [form="♀ (female)"]
  LoLin_v3 = NodeMCU V3.0

nets:
  N1: IC3.Enable_1, IC3.Enable_2, OLED.pin2, LoLin_v3.3V3
  N2: IC3.In_1, LoLin_v3.D6
  N3: IC3.Out_1_(_Controlled_by_Enable_1_), R10.Pin_1, R12.Pin_1
  GND: IC3.0V, Part1.GND, OLED.pin1, LoLin_v3.GND
  N4: IC3.Out_2_(_Controlled_by_Enable_1_), JP1.3
  N5: IC3.In_2, LoLin_v3.D7
  N6: IC3.+Vmotor, IC3.+V, Part1.VOUT
  N7: IC3.In_3, LoLin_v3.D4
  N8: IC3.Out_3_(_Controlled_by_Enable_2_), R9.Pin_1, R11.Pin_1
  N9: IC3.Out_4_(_Controlled_by_Enable_2_), JP1.1
  N10: IC3.In_4, LoLin_v3.D5
  N11: R9.Pin_0, D5.cathode, JP1.2
  N12: R10.Pin_0, D6.cathode, JP1.4
  N13: R11.Pin_0, D5.anode
  N14: R12.Pin_0, D6.anode
  N15: Part1.VIN, LoLin_v3.VU
  N16: OLED.pin3, LoLin_v3.D1
  N17: OLED.pin4, LoLin_v3.D2

notes:
  +
  V1
  V2
  Vout
  Vin
  gnd
  RCA outer
  Gardena v2.20
  SCL SDA

custom parts:
  U3V12F9 9V Step-Up Voltage Regulator: The compact (0.32″×0.515″) U3V12F9 switching step-up (or boost) voltage regulator takes an input voltage as low as 2.5 V and efficiently boosts it to 9 V. The pins have a 0.1″ spacing, making this board compatible with standard solderless breadboards and perfboards.
  NodeMCU V3.0: ESP8266 based NodeMCU
