# Fritzing sketch GardenaDouble_ESP (saved by Fritzing 0.9.3b)
circuit board: 7cm x 5cm
breadboards: 1

parts:
  IC3 = L293D [package=THT]
  R9 = Resistor [tolerance=±5% resistance=100 package=THT]
  R10 = Resistor [tolerance=±5% resistance=100 package=THT]
  R11 = Resistor [tolerance=±5% resistance=10 package=THT]
  R12 = Resistor [tolerance=±5% resistance=10 package=THT]
  D5 = Rectifier Diode [part_number=1N4001 package="300 mil [THT]"]
  D6 = Rectifier Diode [part_number=1N4001 package="300 mil [THT]"]
  JP1 = Header 4 [package=screwterminal-3.5mm-4_lock]
  OLED = Module display OLED I2C 128x64 SSD1306 [package=THT]
  Part1 = U3V12F9 9V Step-Up Voltage Regulator [part_number=U3V12F9]
  LoLin = NodeMCU V3.0

nets:
  VCC: IC3.Enable_1, IC3.Enable_2, OLED.VCC, LoLin.3V3
  N1: IC3.In_1, LoLin.D1
  N2: IC3.Out_1_(_Controlled_by_Enable_1_), R10.Pin_1, R12.Pin_1
  GND: IC3.0V, OLED.GND, Part1.GND, LoLin.GND
  N3: IC3.Out_2_(_Controlled_by_Enable_1_), JP1.3
  N4: IC3.In_2, LoLin.D2
  N5: IC3.+Vmotor, IC3.+V, Part1.VOUT
  N6: IC3.In_3, LoLin.D4
  N7: IC3.Out_3_(_Controlled_by_Enable_2_), R9.Pin_1, R11.Pin_1
  N8: IC3.Out_4_(_Controlled_by_Enable_2_), JP1.1
  N9: IC3.In_4, LoLin.D3
  N10: R9.Pin_0, D5.cathode, JP1.2
  N11: R10.Pin_0, D6.cathode, JP1.4
  N12: R11.Pin_0, D5.anode
  N13: R12.Pin_0, D6.anode
  N14: OLED.SCL, LoLin.D0
  N15: OLED.SDA, LoLin.D5
  N16: Part1.VIN, LoLin.VU

notes:
  +
  V1
  V2
  Vout
  Vin
  gnd
  RCA outer
  Gardena v1.0

custom parts:
  Module display OLED I2C 128x64 SSD1306: Ecran OLED I2C SSD163 de 128x64 avec connexion I2C
  U3V12F9 9V Step-Up Voltage Regulator: The compact (0.32″×0.515″) U3V12F9 switching step-up (or boost) voltage regulator takes an input voltage as low as 2.5 V and efficiently boosts it to 9 V. The pins have a 0.1″ spacing, making this board compatible with standard solderless breadboards and perfboards.
  NodeMCU V3.0: ESP8266 based NodeMCU
